# Fritzing sketch ArduinoDiag (saved by Fritzing 0.9.3b)
breadboards: 2

parts:
  S1 = Pushbutton [package="[THT]"]
  S2 = Pushbutton [package="[THT]"]  # not connected
  S3 = Pushbutton [package="[THT]"]
  LED1 = RGB LED (com. cathode, rgb) [package="5 mm [THT]"]
  R1 = Resistor [tolerance=±5% resistance=330 package=THT]
  R2 = Resistor [tolerance=±5% resistance=330 package=THT]
  R3 = Resistor [tolerance=±5% resistance=330 package=THT]
  R4 = Resistor [tolerance=±5% resistance=10k package=THT]
  R5 = Resistor [tolerance=±5% resistance=10k package=THT]  # not connected
  R6 = Resistor [tolerance=±5% resistance=10k package=THT]  # not connected
  Part1 = Arduino Uno (Rev3)
  J1 = Piezo Speaker
  R7 = PHOTOCELL [package=photocell-kit]
  R8 = Resistor [tolerance=±5% resistance=330 package=THT]
  R10 = Resistor [tolerance=±5% resistance=10k package=THT]
  sds = Resistor [tolerance=±5% resistance=10k package=THT]
  *_Soft-Potentiometer = Rotary Potentiometer (Small) [package=THT]
  R9 = Basic Flex Resistor

nets:
  N1: S1.Pin_1, S1.Pin_2
  N2: S3.Pin_1, S3.Pin_2, LED1.blue_anode, R4.Pin_1, Part1.GND, J1.pin1, R8.Pin_1, sds.Pin_1, *_Soft-Potentiometer.leg1, *_Soft-Potentiometer.leg2, R9.Pin_2
  N3: S3.Pin_3, S3.Pin_4, Part1.D11_PWM/MOSI
  N4: LED1.red_anode, R1.Pin_0, R1.Pin_1
  N5: LED1.common_cathode, R2.Pin_1
  N6: R3.Pin_0, R3.Pin_1, Part1.5V, R7.P$1, R10.Pin_0
  N7: Part1.A0, sds.Pin_0, *_Soft-Potentiometer.wiper
  N8: Part1.A1, R10.Pin_1, R9.pin_1
  N9: Part1.A2, R7.P$2, R8.Pin_0
  N10: Part1.D8, J1.pin2
